// Logisim project microOrgaSmall.circ as structural Verilog: 7 circuits, main circuit microOrgaSmall
module microOrgaSmall (
  input  in_1,
  input  in_2,
  output C,
  output Z,
  output N
);

  wire ALU_enA, ALU_enB, ALU_enOut, ALU_opW, button_1_out, button_2_out, button_3_out, clk, clock_1_out, clr,
       DE_enOutImm, DE_loadH, DE_loadL, MM_enAddr, MM_enOut, MM_load, PC_enOut, PC_inc, PC_load, RB_enIn,
       RB_enOut, RB_selectIndexIn, RB_selectIndexOut, rst;
  wire [2:0] multiplexer_1_out, multiplexer_2_out, X, Y;
  wire [3:0] ALU_OP;
  wire [4:0] OP;
  wire [7:0] A, B, controlled_buffer_1_out, M, O, PC_v;
  wire [8:0] microPC_out;
  wire [15:0] INST;
  wire [31:0] R0_to_R3, R4_to_R7;

  assign controlled_buffer_1_out = DE_enOutImm ? M : 8'bz;  // Controlled_Buffer controlled_buffer_1
  PC pc_1 (
    .VIEW_value(PC_v), .outValue(controlled_buffer_1_out), .Load(PC_load), .Inc(PC_inc), .clk(clk),
    .rst(rst), .inData(controlled_buffer_1_out), .enableOut(PC_enOut));
  Registers registers_1 (
    .outData(controlled_buffer_1_out), .R0_to_R3(R0_to_R3), .R4_to_R7(R4_to_R7),
    .outSelect(multiplexer_2_out), .enOut(RB_enOut), .clk(clk), .rst(rst), .enableIn(RB_enIn),
    .inSelect(multiplexer_1_out), .inData(controlled_buffer_1_out));
  Memory memory_1 (
    .outValue(controlled_buffer_1_out), .Load(MM_load), .clk(clk), .rst(rst), .clr(clr),
    .enableAddress(MM_enAddr), .Address(controlled_buffer_1_out), .inData(controlled_buffer_1_out),
    .enableOut(MM_enOut));
  Decode decode_1 (
    .opCode(OP), .indexX(X), .indexY(Y), .valueM(M), .VIEW_Instr(INST), .clk(clk), .rst(rst),
    .load_low(DE_loadL), .load_high(DE_loadH), .Half_Instruction(controlled_buffer_1_out));
  Multiplexer #(.width(3)) multiplexer_1 (
    .in0(X), .in1(Y), .out(multiplexer_1_out), .sel(RB_selectIndexIn));  // open: en
  Multiplexer #(.width(3)) multiplexer_2 (
    .in0(X), .in1(Y), .out(multiplexer_2_out), .sel(RB_selectIndexOut));  // open: en
  ALU alu_1 (
    .ALU_OUT(controlled_buffer_1_out), .VIEW_out(O), .Flags({N, Z, C}), .VIEW_A(A), .VIEW_B(B),
    .opW(ALU_opW), .enOut(ALU_enOut), .enA(ALU_enA), .enB(ALU_enB), .rst(rst), .clk(clk),
    .A(controlled_buffer_1_out), .B(controlled_buffer_1_out), .shift(Y), .OP(ALU_OP));
  ControlUnit controlunit_1 (
    .ALU_OP(ALU_OP), .MM_enOut(MM_enOut), .MM_load(MM_load), .MM_enAddr(MM_enAddr), .ALU_enA(ALU_enA),
    .ALU_enB(ALU_enB), .ALU_enOut(ALU_enOut), .ALU_opW(ALU_opW), .RB_enIn(RB_enIn), .PC_load(PC_load),
    .PC_inc(PC_inc), .RB_enOut(RB_enOut), .PC_enOut(PC_enOut), .DE_enOutImm(DE_enOutImm),
    .DE_loadL(DE_loadL), .DE_loadH(DE_loadH), .RB_selectIndexIn(RB_selectIndexIn),
    .RB_selectIndexOut(RB_selectIndexOut), .VIEW_microOpAddr(microPC_out), .OP_code(OP), .flags({N, Z, C}),
    .clk(clk), .rst(rst));
  Hex_Digit_Display hex_digit_display_1 (.value(INST[11:8]));  // open: dp
  Hex_Digit_Display hex_digit_display_2 (.value(INST[15:12]));  // open: dp
  Hex_Digit_Display hex_digit_display_3 (.value(M[7:4]));  // open: dp
  Hex_Digit_Display hex_digit_display_4 (.value(R0_to_R3[7:4]));  // open: dp
  Hex_Digit_Display hex_digit_display_5 (.value(R0_to_R3[3:0]));  // open: dp
  Hex_Digit_Display hex_digit_display_6 (.value(R0_to_R3[11:8]));  // open: dp
  Hex_Digit_Display hex_digit_display_7 (.value(R0_to_R3[15:12]));  // open: dp
  Hex_Digit_Display hex_digit_display_8 (.value(R0_to_R3[19:16]));  // open: dp
  Hex_Digit_Display hex_digit_display_9 (.value(R0_to_R3[23:20]));  // open: dp
  Hex_Digit_Display hex_digit_display_10 (.value(R0_to_R3[31:28]));  // open: dp
  Hex_Digit_Display hex_digit_display_11 (.value(R0_to_R3[27:24]));  // open: dp
  Hex_Digit_Display hex_digit_display_12 (.value(INST[7:4]));  // open: dp
  Hex_Digit_Display hex_digit_display_13 (.value(M[3:0]));  // open: dp
  Button button_1 (.out(button_1_out));
  Clock clock_1 (.out(clock_1_out));
  Hex_Digit_Display hex_digit_display_14 (.value(INST[3:0]));  // open: dp
  Hex_Digit_Display hex_digit_display_15 (.value({1'b0, X}));  // open: dp
  or or_1 (clk, button_1_out, clock_1_out);
  Hex_Digit_Display hex_digit_display_16 (.value(R4_to_R7[7:4]));  // open: dp
  Hex_Digit_Display hex_digit_display_17 (.value(R4_to_R7[15:12]));  // open: dp
  Hex_Digit_Display hex_digit_display_18 (.value(R4_to_R7[23:20]));  // open: dp
  Hex_Digit_Display hex_digit_display_19 (.value(R4_to_R7[31:28]));  // open: dp
  Button button_2 (.out(button_2_out));
  or or_2 (rst, button_2_out, in_1);
  Hex_Digit_Display hex_digit_display_20 (.value(R4_to_R7[3:0]));  // open: dp
  Hex_Digit_Display hex_digit_display_21 (.value(R4_to_R7[11:8]));  // open: dp
  Hex_Digit_Display hex_digit_display_22 (.value(R4_to_R7[19:16]));  // open: dp
  Hex_Digit_Display hex_digit_display_23 (.value(R4_to_R7[27:24]));  // open: dp
  Hex_Digit_Display hex_digit_display_24 (.value(microPC_out[7:4]));  // open: dp
  Hex_Digit_Display hex_digit_display_25 (.value({3'b000, microPC_out[8]}));  // open: dp
  Hex_Digit_Display hex_digit_display_26 (.value({1'b0, Y}));  // open: dp
  Button button_3 (.out(button_3_out));
  Hex_Digit_Display hex_digit_display_27 (.value(PC_v[7:4]));  // open: dp
  Hex_Digit_Display hex_digit_display_28 (.value(A[7:4]));  // open: dp
  Hex_Digit_Display hex_digit_display_29 (.value(B[7:4]));  // open: dp
  Hex_Digit_Display hex_digit_display_30 (.value(O[7:4]));  // open: dp
  Hex_Digit_Display hex_digit_display_31 (.value(microPC_out[3:0]));  // open: dp
  Hex_Digit_Display hex_digit_display_32 (.value({3'b000, OP[4]}));  // open: dp
  or or_3 (clr, button_3_out, in_2);
  Hex_Digit_Display hex_digit_display_33 (.value(PC_v[3:0]));  // open: dp
  Hex_Digit_Display hex_digit_display_34 (.value(A[3:0]));  // open: dp
  Hex_Digit_Display hex_digit_display_35 (.value(B[3:0]));  // open: dp
  Hex_Digit_Display hex_digit_display_36 (.value(O[3:0]));  // open: dp
  Hex_Digit_Display hex_digit_display_37 (.value(OP[3:0]));  // open: dp

  // Other names for the same wires on the sheet: flags[2:0] = {N, Z, C}

  // Notes on the sheet:
  //   X
  //   Instruction
  //   R0
  //   R1
  //   R2
  //   R3
  //   M value
  //   index X
  //   R4
  //   R5
  //   R6
  //   R7
  //   microPC
  //   index Y
  //   Opcode
  //   PC
  //   A
  //   B
  //   OUT
endmodule

module Registers (
  input  [7:0] inData,
  input  clk,
  input  rst,
  input  enOut,
  input  enableIn,
  input  [2:0] outSelect,
  input  [2:0] inSelect,
  output [31:0] R0_to_R3,
  output [31:0] R4_to_R7,
  output [7:0] outData
);

  wire decoder_1_out0, decoder_1_out1, decoder_1_out2, decoder_1_out3, decoder_1_out4, decoder_1_out5,
       decoder_1_out6, decoder_1_out7;
  wire [7:0] multiplexer_1_out;

  Decoder #(.select(3)) decoder_1 (
    .out0(decoder_1_out0), .out1(decoder_1_out1), .out2(decoder_1_out2), .out3(decoder_1_out3),
    .out4(decoder_1_out4), .out5(decoder_1_out5), .out6(decoder_1_out6), .out7(decoder_1_out7),
    .sel(inSelect), .en(enableIn));
  Register R0 (.D(inData), .en(decoder_1_out0), .Q(R0_to_R3[7:0]), .clk(clk), .clr(rst));
  Register R1 (.D(inData), .en(decoder_1_out1), .Q(R0_to_R3[15:8]), .clk(clk), .clr(rst));
  Register R2 (.D(inData), .en(decoder_1_out2), .Q(R0_to_R3[23:16]), .clk(clk), .clr(rst));
  Register R3 (.D(inData), .en(decoder_1_out3), .Q(R0_to_R3[31:24]), .clk(clk), .clr(rst));
  Register R4 (.D(inData), .en(decoder_1_out4), .Q(R4_to_R7[7:0]), .clk(clk), .clr(rst));
  Register R5 (.D(inData), .en(decoder_1_out5), .Q(R4_to_R7[15:8]), .clk(clk), .clr(rst));
  Register R6 (.D(inData), .en(decoder_1_out6), .Q(R4_to_R7[23:16]), .clk(clk), .clr(rst));
  Register R7 (.D(inData), .en(decoder_1_out7), .Q(R4_to_R7[31:24]), .clk(clk), .clr(rst));
  Multiplexer #(.select(3), .width(8)) multiplexer_1 (
    .in0(R0_to_R3[7:0]), .in1(R0_to_R3[15:8]), .in2(R0_to_R3[23:16]), .in3(R0_to_R3[31:24]),
    .in4(R4_to_R7[7:0]), .in5(R4_to_R7[15:8]), .in6(R4_to_R7[23:16]), .in7(R4_to_R7[31:24]),
    .out(multiplexer_1_out), .sel(outSelect));  // open: en
  assign outData = enOut ? multiplexer_1_out : 8'bz;  // Controlled_Buffer controlled_buffer_1

  // Notes on the sheet:
  //   X
endmodule

module PC (
  input  clk,
  input  rst,
  input  Load,
  input  [7:0] inData,
  input  Inc,
  input  enableOut,
  output [7:0] VIEW_value,
  output [7:0] outValue
);

  Counter counter_1 (.load(Load), .D(inData), .count(Inc), .Q(VIEW_value), .clk(clk), .clr(rst));  // open: carry
  assign outValue = enableOut ? VIEW_value : 8'bz;  // Controlled_Buffer controlled_buffer_1

  // Notes on the sheet:
  //   X
endmodule

module ALU (
  input  clk,
  input  rst,
  input  [7:0] A,
  input  enA,
  input  [7:0] B,
  input  enB,
  input  opW,
  input  enOut,
  input  [2:0] shift,
  input  [3:0] OP,
  output [2:0] Flags,
  output [7:0] ALU_OUT,
  output [7:0] VIEW_out,
  output [7:0] VIEW_A,
  output [7:0] VIEW_B
);

  wire adder_1_cout, adder_2_cout, multiplexer_1_out, nor_1_out, or_2_out, subtractor_1_bout,
       subtractor_2_bout;
  wire [7:0] adder_1_out, adder_2_out, and_1_out, multiplexer_2_out, or_1_out, shifter_1_out, shifter_2_out,
       subtractor_1_out, subtractor_2_out, xor_1_out;

  Register ALU_IN_A (.D(A), .en(enA), .Q(VIEW_A), .clk(clk), .clr(rst));
  Register ALU_IN_B (.D(B), .en(enB), .Q(VIEW_B), .clk(clk), .clr(rst));
  Adder adder_1 (.a(VIEW_A), .b(VIEW_B), .out(adder_1_out), .cin(1'b0), .cout(adder_1_cout));
  Adder adder_2 (.a(VIEW_A), .b(VIEW_B), .out(adder_2_out), .cin(Flags[0]), .cout(adder_2_cout));
  Subtractor subtractor_1 (.a(VIEW_A), .b(VIEW_B), .out(subtractor_1_out), .bin(1'b0), .bout(subtractor_1_bout));
  assign and_1_out = VIEW_A & VIEW_B;  // AND_Gate and_1, 8 bits wide
  assign or_1_out = VIEW_A | VIEW_B;  // OR_Gate or_1, 8 bits wide
  assign xor_1_out = VIEW_A ^ VIEW_B;  // XOR_Gate xor_1, 8 bits wide
  Subtractor subtractor_2 (.a(VIEW_A), .b(VIEW_B), .out(subtractor_2_out), .bin(1'b0), .bout(subtractor_2_bout));
  Shifter shifter_1 (.in(VIEW_A), .\dist (shift), .out(shifter_1_out));
  Shifter #(.shift("lr")) shifter_2 (.in(VIEW_A), .\dist (shift), .out(shifter_2_out));
  Multiplexer #(.select(4)) multiplexer_1 (
    .in0(1'b0), .in1(adder_1_cout), .in2(adder_2_cout), .in3(subtractor_1_bout), .in4(1'b0), .in5(1'b0),
    .in6(1'b0), .in7(subtractor_2_bout), .in8(1'b0), .in9(1'b0), .in10(1'b0), .in11(1'b0), .in12(1'b0),
    .in13(1'b0), .in14(1'b0), .in15(1'b0), .out(multiplexer_1_out), .sel(OP));  // open: en
  Register #(.width(1), .trigger("falling")) C (.D(multiplexer_1_out), .en(opW), .Q(Flags[0]), .clk(clk), .clr(rst));
  nor nor_1 (nor_1_out, multiplexer_2_out[0], multiplexer_2_out[1], multiplexer_2_out[2], multiplexer_2_out[3], multiplexer_2_out[4], multiplexer_2_out[5], multiplexer_2_out[6], multiplexer_2_out[7]);
  Multiplexer #(.select(4), .width(8)) multiplexer_2 (
    .in0({8{1'b0}}), .in1(adder_1_out), .in2(adder_2_out), .in3(subtractor_1_out), .in4(and_1_out),
    .in5(or_1_out), .in6(xor_1_out), .in7(subtractor_2_out), .in8(shifter_1_out), .in9(shifter_2_out),
    .in10({8{1'b0}}), .in11({8{1'b0}}), .in12({8{1'b0}}), .in13(8'h1), .in14(8'h2), .in15({8{1'b1}}),
    .out(multiplexer_2_out), .sel(OP));  // open: en
  Register #(.width(1), .trigger("falling")) Z (.D(nor_1_out), .en(opW), .Q(Flags[1]), .clk(clk), .clr(rst));
  or or_2 (or_2_out, OP[3], OP[2], OP[1], OP[0]);
  Register #(.trigger("falling")) ALU_REG_OUT (
    .D(multiplexer_2_out), .en(or_2_out), .Q(VIEW_out), .clk(clk), .clr(rst));
  Register #(.width(1), .trigger("falling")) N (.D(multiplexer_2_out[7]), .en(opW), .Q(Flags[2]), .clk(clk), .clr(rst));
  assign ALU_OUT = enOut ? VIEW_out : 8'bz;  // Controlled_Buffer controlled_buffer_1

  // Other names for the same wires on the sheet: write_op = opW

  // Notes on the sheet:
  //   X
  //   ADD = 0001
  //   ADC = 0010
  //   SUB = 0011
  //   AND = 0100
  //   OR = 0101
  //   XOR = 0110
  //   CMP = 0111
  //   SHR = 1000
  //   SHL = 1001
  //   CONSTANTES
  //   CTE 0x00 = 1100
  //   CTE 0x01 = 1101
  //   CTE 0x02 = 1110
  //   CTE 0xFF = 1111
endmodule

module Memory (
  input  clk,
  input  rst,
  input  clr,
  input  [7:0] Address,
  input  enableAddress,
  input  [7:0] inData,
  input  Load,
  input  enableOut,
  output [7:0] outValue
);

  wire [7:0] ram_1_data, register_1_q;

  Register register_1 (.D(Address), .en(enableAddress), .Q(register_1_q), .clk(clk), .clr(rst));
  RAM ram_1 (.addr(register_1_q), .data(ram_1_data), .clk(clk), .ld(Load), .clr(clr));  // open: sel
  assign outValue = enableOut ? ram_1_data : 8'bz;  // Controlled_Buffer controlled_buffer_1

  // Notes on the sheet:
  //   X
endmodule

module Decode (
  input  clk,
  input  rst,
  input  [7:0] Half_Instruction,
  input  load_low,
  input  load_high,
  output [4:0] opCode,
  output [2:0] indexX,
  output [2:0] indexY,
  output [7:0] valueM,
  output [15:0] VIEW_Instr
);

  Register register_1 (.D(Half_Instruction), .en(load_low), .Q(VIEW_Instr[7:0]), .clk(clk), .clr(rst));
  Register register_2 (.D(Half_Instruction), .en(load_high), .Q(VIEW_Instr[15:8]), .clk(clk), .clr(rst));
  Register #(.width(5)) register_3 (.D(VIEW_Instr[15:11]), .Q(opCode), .clk(clk), .clr(rst));  // open: en
  Register #(.width(3)) register_4 (.D(VIEW_Instr[10:8]), .Q(indexX), .clk(clk), .clr(rst));  // open: en
  Register #(.width(3)) register_5 (.D(VIEW_Instr[7:5]), .Q(indexY), .clk(clk), .clr(rst));  // open: en
  Register register_6 (.D(VIEW_Instr[7:0]), .Q(valueM), .clk(clk), .clr(rst));  // open: en

  // Notes on the sheet:
  //   X
endmodule

module ControlUnit (
  input  clk,
  input  rst,
  input  [2:0] flags,
  input  [4:0] OP_code,
  output RB_enIn,
  output [8:0] VIEW_microOpAddr,
  output RB_enOut,
  output RB_selectIndexIn,
  output RB_selectIndexOut,
  output MM_enOut,
  output MM_load,
  output MM_enAddr,
  output ALU_enA,
  output ALU_enB,
  output ALU_enOut,
  output ALU_opW,
  output [3:0] ALU_OP,
  output PC_load,
  output PC_inc,
  output PC_enOut,
  output DE_enOutImm,
  output DE_loadL,
  output DE_loadH
);

  wire and_1_out, and_2_out, and_3_out, jc_microOp, jn_microOp, jz_microOp, load_microOp, not_1_out,
       or_1_out, or_2_out, or_3_out, reset_microOp;
  wire [8:0] adder_1_out, adder_2_out, multiplexer_1_out, multiplexer_2_out;
  wire [29:7] rom_1_data;

  not not_1 (not_1_out, load_microOp);
  Multiplexer #(.width(9)) multiplexer_1 (
    .in0({OP_code, 4'b0000}), .in1(multiplexer_2_out), .out(multiplexer_1_out), .sel(or_2_out));  // open: en
  Counter #(.width(9), .max('h1ff)) microPC (
    .load(load_microOp), .D(multiplexer_1_out), .count(not_1_out), .Q(VIEW_microOpAddr), .clk(clk),
    .clr(or_1_out));  // open: carry
  or or_1 (or_1_out, reset_microOp, rst);
  or or_2 (or_2_out, jn_microOp, jz_microOp, jc_microOp);
  and and_1 (and_1_out, jc_microOp, flags[0]);
  and and_2 (and_2_out, jz_microOp, flags[1]);
  and and_3 (and_3_out, jn_microOp, flags[2]);
  Adder #(.width(9)) adder_1 (.a(VIEW_microOpAddr), .b(9'h1), .out(adder_1_out));  // open: cin, cout
  Adder #(.width(9)) adder_2 (.a(VIEW_microOpAddr), .b(9'h2), .out(adder_2_out));  // open: cin, cout
  Multiplexer #(.width(9)) multiplexer_2 (
    .in0(adder_1_out), .in1(adder_2_out), .out(multiplexer_2_out), .sel(or_3_out));  // open: en
  or or_3 (or_3_out, and_1_out, and_2_out, and_3_out);
  ROM #(.addrWidth(9), .dataWidth(32)) rom_1 (
    .addr(VIEW_microOpAddr),
    .data({reset_microOp, load_microOp, rom_1_data[29:27], DE_loadH, DE_loadL, DE_enOutImm, rom_1_data[23], PC_enOut, PC_inc, PC_load, rom_1_data[19], jn_microOp, jz_microOp, jc_microOp, ALU_OP, ALU_opW, ALU_enOut, ALU_enB, ALU_enA, rom_1_data[7], MM_enAddr, MM_load, MM_enOut, RB_selectIndexOut, RB_selectIndexIn, RB_enOut, RB_enIn}));  // open: sel

  // Notes on the sheet:
  //   X
endmodule
